# Fritzing sketch NeoPixelClock (saved by Fritzing 0.8.7b)
breadboards: 2

parts:
  FLORA1 = Adafruit_Flora
  neopixel1 = Neopixel 24 Ring
  U1 = LIPO-1000mAh [package=lipo-1000]
  C1 = Electrolytic Capacitor [capacitance=1000μF package="1010 [SMD, electrolytic]"]
  R1 = Resistor [tolerance=±5% resistance=330 package=THT]
  SP1 = SPEAKER [package=pcb_mount_speaker]
  JP1 = Header 2 [package=jst-2-pth-kit]
  S1 = JOYSTICK_MINI [package=joystick_mini]

nets:
  N1: FLORA1.connector1, neopixel1.GND
  N2: FLORA1.connector2, S1.LEFT
  N3: FLORA1.connector3, S1.RIGHT
  N4: FLORA1.connector4, neopixel1.Vcc
  N5: FLORA1.connector5, S1.UP
  N6: FLORA1.connector6, S1.DOWN
  N7: FLORA1.connector9, S1.GND
  N8: FLORA1.connector11, U1.-, C1.+, SP1.+, JP1.2
  N9: FLORA1.connector12, SP1.-
  N10: FLORA1.connector13, R1.Pin_0
  N11: neopixel1.IN, R1.Pin_1
  N12: U1.+, C1.-, JP1.1
